# Fritzing sketch Rotary_Sensor (saved by Fritzing 0.9.3b)
circuit board: 8.46667cm x 5.64444cm

parts:
  SN_9553034323535140E130 = Arduino Uno (Rev3) [part_number="Mon numéro de série"]
  R1 = Rotary Potentiometer (Small) [maximum_resistance=10kΩ package=THT]

nets:
  N1: SN_9553034323535140E130.A0, R1.wiper
  N2: SN_9553034323535140E130.GND, R1.leg1
  N3: SN_9553034323535140E130.5V, R1.leg2

// code stored in the sketch: rotary_sensor.ino
/* 

http://wiki.seeed.cc/Grove-Rotary_Angle_Sensor/ 

/*macro definitions of Rotary angle sensor and LED pin*/
    #define ROTARY_ANGLE_SENSOR A0
    #define LED 2//the Grove - LED is connected to D3 of Arduino
    #define ADC_REF 5//reference voltage of ADC is 5v.If the Vcc switch on the seeeduino
                     //board switches to 3V3, the ADC_REF should be 3.3
    #define GROVE_VCC 5//VCC of the grove interface is normally 5v
    #define FULL_ANGLE 300//full value of the rotary angle is 300 degrees

*/

void setup() {
  // put your setup code here, to run once:
	Serial.begin(9600);
  pinsInit();

}

void loop() {
  // put your main code here, to run repeatedly:

int degrees;
        degrees = getDegree();
        Serial.println("The angle between the mark and the starting position:");
        Serial.println(degrees);

			 Serial.println(brightness);

        int brightness;
        /*The degrees is 0~300, should be converted to be 0~255 to control the*/
        /*brightness of LED                                                   */
        brightness = map(degrees, 0, FULL_ANGLE, 0, 255); 
        controlBrightness(brightness);

        delay(500);

}
void pinsInit()
    {
        pinMode(ROTARY_ANGLE_SENSOR, INPUT);
        pinMode(LED,OUTPUT);
    }

    /*PWM control brightness                        */
    /*If brightness is 0,the LED is off.            */
    /*The Greater the brightness, the brighter the LED.*/
    /*The range of brightness is 0~255              */
    void controlBrightness(int brightness)
    {
        analogWrite(LED,brightness);
    }
    /************************************************************************/
    /*Function: Get the angle between the mark and the starting position    */
    /*Parameter:-void                                                       */
    /*Return:   -int,the range of degrees is 0~300                          */
    int getDegree()
    {
        int sensor_value = analogRead(ROTARY_ANGLE_SENSOR);
        float voltage;
        voltage = (float)sensor_value*ADC_REF/1023;
        float degrees = (voltage*FULL_ANGLE)/GROVE_VCC;
        return degrees;
    }
